# Fritzing sketch Nachtlicht (saved by Fritzing 0.9.3b)
circuit board: 6.88566cm x 5.36311cm
breadboards: 1

parts:
  R5 = Photocell (LDR) [package=THT]
  LED3 = LED - 5mm [color="Red (633nm)" package="5 mm [THT]"]
  R6 = Resistor [tolerance=±5% resistance=10k package=THT]
  Arduino1 = Arduino Uno (Rev3)
  R7 = Resistor [tolerance=±5% resistance=220 package=THT]  # not connected

nets (from the schematic view):
  N1: R5.pin_0, Arduino1.5V
  N2: R5.pin_1, R6.Pin_0, Arduino1.A2
  N3: LED3.cathode, Arduino1.D13/SCK
  N4: LED3.anode, R6.Pin_1, Arduino1.GND

notes:
  Nachtlicht
  ---------------
  Aufbau für 3 Experimente:
  1. DIM Funktion einer LED, die langsam heller wird
  2. LDR auslesen
  3. ein Nachtlicht, LED geht an wenn LDR einen bestimmten werd liefert, dieser Wert wird auf die LED übertragen
