# Fritzing sketch Photocell (saved by Fritzing 0.9.3b)
circuit board: 6.88566cm x 5.36311cm
breadboards: 2

parts:
  R5 = Photocell (LDR) [package=THT]
  LED3 = LED - 5mm [color="Red (633nm)" package="5 mm [THT]"]
  R6 = Resistor [tolerance=±5% resistance=10k package=THT]
  Arduino1 = Arduino Uno (Rev3)

nets:
  N1: R5.pin_0, Arduino1.5V
  N2: R5.pin_1, R6.Pin_0, Arduino1.A2
  N3: LED3.cathode, Arduino1.D13/SCK
  N4: LED3.anode, R6.Pin_1, Arduino1.GND
