# Fritzing sketch Blink (saved by Fritzing 0.9.3b)
circuit board: 6.88566cm x 5.36311cm

parts:
  LED = LED - 5mm [color="Red (633nm)" package="5 mm [THT]"]
  Arduino1 = Arduino Uno (Rev3)

nets:
  N1: LED.cathode, Arduino1.GND
  N2: LED.anode, Arduino1.D13/SCK

notes:
  BLINK

// code stored in the sketch: Blink.ino
int led = 10;                   

void setup() { 
  pinMode(led, OUTPUT);     
}

void loop() {                   
  digitalWrite(led, HIGH);      
  delay(1000);                  
  digitalWrite(led, LOW);       
  delay(1000);               
}
