# Fritzing sketch blinkiMitTaster (saved by Fritzing 0.9.3b)
circuit board: 8.46667cm x 5.64444cm
breadboards: 1

parts:
  LED1 = LED - 5mm [color="Red (633nm)" package="5 mm [THT]"]
  S1 = Pushbutton [package="[THT]"]
  R1 = Resistor [tolerance=±5% resistance=10k package=THT]
  Bauteil1 = Arduino Uno (Rev3)

nets:
  N1: LED1.cathode, R1.Pin_1, Bauteil1.GND
  N2: LED1.anode, Bauteil1.D13/SCK
  N3: S1.Pin_1, S1.Pin_2, S1.Pin_3, S1.Pin_4, R1.Pin_0, Bauteil1.D7, Bauteil1.3V3

notes:
  der Taster braucht 3 Kabel:
  1. rot 3.3 V
  2. schwarz R10K + GND
  3. Input PIN 7
