# Fritzing sketch LEDMatrix3x3 (saved by Fritzing 0.9.3b)
breadboards: 1

parts:
  LED3 = LED - 5mm [color="Yellow (595nm)" package="5 mm [THT]"]
  LED2 = LED - 5mm [color="Yellow (595nm)" package="5 mm [THT]"]
  LED1 = LED - 5mm [color="Yellow (595nm)" package="5 mm [THT]"]
  LED6 = LED - 5mm [color="Red (660nm)" package="5 mm [THT]"]
  LED5 = LED - 5mm [color="Red (660nm)" package="5 mm [THT]"]
  LED8 = LED - 5mm [color="Green (570nm)" package="5 mm [THT]"]
  R2 = Resistor [tolerance=±5% resistance=220 package=THT]
  R3 = Resistor [tolerance=±5% resistance=220 package=THT]
  R4 = Resistor [tolerance=±5% resistance=220 package=THT]
  LED9 = LED - 5mm [color="Green (570nm)" package="5 mm [THT]"]
  Bauteil1 = Arduino Uno (Rev3)
  LED4 = LED - 5mm [color="Red (633nm)" package="5 mm [THT]"]
  LED7 = LED - 5mm [color="Green (570nm)" package="5 mm [THT]"]

nets (from the schematic view):
  N1: LED3.cathode, LED6.cathode, R3.Pin_0
  N2: LED3.anode, LED1.anode, Bauteil1.D5_PWM
  N3: LED2.cathode, LED5.cathode, LED8.cathode, R2.Pin_0
  N4: LED1.cathode, R4.Pin_1, LED4.cathode, LED7.cathode
  N5: LED6.anode, LED5.anode, Bauteil1.D6_PWM, LED4.anode
  N6: LED8.anode, LED9.anode, Bauteil1.D7, LED7.anode
  N7: R2.Pin_1, Bauteil1.D9_PWM
  N8: R3.Pin_1, Bauteil1.D8
  N9: R4.Pin_0, Bauteil1.D10_PWM/SS
